// Digital circuit keboard_decode_display_test.dig as structural Verilog
module keboard_decode_display_test (
  input  En,
  input  Diff,
  input  in_3,
  input  in_4,
  input  in_5,
  input  in_6,
  input  in_7,
  input  in_8,
  input  in_9,
  input  in_10,
  input  clr
);

  wire not_1_out, not_2_out;
  wire [7:0] multiplexer_1_out, u_BCD_2_decoder_seg, u_BIN_decoder_seg;

  BCD_2_decoder #(.applicationType("GHDL")) u_BCD_2_decoder (
    .EN(En), .CLR(clr), .BCD({in_3, in_4, in_5, in_6, in_7, in_8, in_9, in_10}), .Seg(u_BCD_2_decoder_seg));  // open: Value
  BIN_decoder #(.applicationType("GHDL")) u_BIN_decoder (
    .EN(En), .CLR(clr), .BIN({in_3, in_4, in_5, in_6, in_7, in_8, in_9, in_10}), .Seg(u_BIN_decoder_seg));  // open: Value
  Seven_Seg_Hex seven_seg_hex_1 (.d(multiplexer_1_out[7:4]), .dp(1'b0));
  Multiplexer #(.Bits(8)) multiplexer_1 (
    .sel(Diff), .in_0(u_BCD_2_decoder_seg), .in_1(u_BIN_decoder_seg), .out(multiplexer_1_out));
  Seven_Seg_Hex seven_seg_hex_2 (.d(multiplexer_1_out[3:0]), .dp(1'b0));
  not not_1 (not_1_out, Diff);
  not not_2 (not_2_out, Diff);
  Seven_Seg seven_seg_1 (.a(not_1_out), .b(Diff), .c(Diff), .d(not_2_out), .e(1'b1), .f(1'b1), .g(1'b1), .dp(1'b0));

  // Notes on the sheet:
  //   Enter Password
  //   Entered
  //   Enter
  //   Difficulty
endmodule

/* Code of BCD_2_decoder:
library IEEE;
use IEEE.STD_LOGIC_1164.ALL;
use IEEE.NUMERIC_STD.ALL;

entity BCD_2_decoder is
    Port (
        EN    : in  STD_LOGIC;
        CLR   : in  STD_LOGIC;
        BCD   : in  STD_LOGIC_VECTOR(7 downto 0);
        Value : out STD_LOGIC_VECTOR(6 downto 0);
        Seg   : out STD_LOGIC_VECTOR(7 downto 0)  -- High 4-bits: Tens, Low 4-bits: Units
    );
end BCD_2_decoder;

architecture Behavioral of BCD_2_decoder is
begin
    process(EN, CLR, BCD)
        variable tens_val  : integer range 0 to 15;
        variable units_val : integer range 0 to 15;
        variable bin_val   : integer range 0 to 127;
    begin
        tens_val  := to_integer(unsigned(BCD(7 downto 4)));
        units_val := to_integer(unsigned(BCD(3 downto 0)));
        bin_val   := (tens_val * 10) + units_val;
        
        if EN = '0' or CLR = '1' then
            Value <= (others => '0');
            Seg   <= (others => '0');
        else
            Value <= std_logic_vector(to_unsigned(bin_val, 7));
            Seg   <= BCD; -- Since BCD input is already two 4-bit numbers (tens & units)!
        end if;
    end process;
end Behavioral;
*/

/* Code of BIN_decoder:
library IEEE;
use IEEE.STD_LOGIC_1164.ALL;
use IEEE.NUMERIC_STD.ALL;

entity BIN_decoder is
    Port (
        EN    : in  STD_LOGIC;
        CLR   : in  STD_LOGIC;
        BIN   : in  STD_LOGIC_VECTOR(7 downto 0);
        Value : out STD_LOGIC_VECTOR(7 downto 0);
        Seg   : out STD_LOGIC_VECTOR(7 downto 0)  -- High 4-bits: Tens, Low 4-bits: Units
    );
end BIN_decoder;

architecture Behavioral of BIN_decoder is
begin
    process(EN, CLR, BIN)
        variable bin_val   : integer range 0 to 255;
        variable tens_int  : integer range 0 to 31;
        variable units_int : integer range 0 to 15;
    begin
        bin_val := to_integer(unsigned(BIN));
        
        if EN = '0' or CLR = '1' then
            Value <= (others => '0');
            Seg   <= (others => '0');
        else
            Value <= BIN;
            
            tens_int  := bin_val / 10;
            units_int := bin_val mod 10;
            
            Seg <= std_logic_vector(to_unsigned(tens_int, 4)) & std_logic_vector(to_unsigned(units_int, 4));
        end if;
    end process;

end Behavioral;
*/
