// Digital circuit led_rom_test.dig as structural Verilog
module led_rom_test (
  input  En,
  input  [1:0] Mode,
  input  [3:0] Progress
);

  wire [47:0] u_ROM_LED_Arranger_data;

  ROM_LED_Arranger #(.applicationType("GHDL")) u_ROM_LED_Arranger (
    .EN(En), .Mode(Mode), .Progress(Progress), .Data(u_ROM_LED_Arranger_data));
  LED led_1 (.in(u_ROM_LED_Arranger_data[23]));
  LED led_2 (.in(u_ROM_LED_Arranger_data[47]));
  LED led_3 (.in(u_ROM_LED_Arranger_data[22]));
  LED led_4 (.in(u_ROM_LED_Arranger_data[21]));
  LED led_5 (.in(u_ROM_LED_Arranger_data[46]));
  LED led_6 (.in(u_ROM_LED_Arranger_data[45]));
  LED led_7 (.in(u_ROM_LED_Arranger_data[20]));
  LED led_8 (.in(u_ROM_LED_Arranger_data[19]));
  LED led_9 (.in(u_ROM_LED_Arranger_data[44]));
  LED led_10 (.in(u_ROM_LED_Arranger_data[43]));
  LED led_11 (.in(u_ROM_LED_Arranger_data[17]));
  LED led_12 (.in(u_ROM_LED_Arranger_data[18]));
  LED led_13 (.in(u_ROM_LED_Arranger_data[41]));
  LED led_14 (.in(u_ROM_LED_Arranger_data[42]));
  LED led_15 (.in(u_ROM_LED_Arranger_data[16]));
  LED led_16 (.in(u_ROM_LED_Arranger_data[15]));
  LED led_17 (.in(u_ROM_LED_Arranger_data[40]));
  LED led_18 (.in(u_ROM_LED_Arranger_data[39]));
  LED led_19 (.in(u_ROM_LED_Arranger_data[14]));
  LED led_20 (.in(u_ROM_LED_Arranger_data[13]));
  LED led_21 (.in(u_ROM_LED_Arranger_data[38]));
  LED led_22 (.in(u_ROM_LED_Arranger_data[37]));
  LED led_23 (.in(u_ROM_LED_Arranger_data[11]));
  LED led_24 (.in(u_ROM_LED_Arranger_data[12]));
  LED led_25 (.in(u_ROM_LED_Arranger_data[35]));
  LED led_26 (.in(u_ROM_LED_Arranger_data[36]));
  LED led_27 (.in(u_ROM_LED_Arranger_data[9]));
  LED led_28 (.in(u_ROM_LED_Arranger_data[10]));
  LED led_29 (.in(u_ROM_LED_Arranger_data[33]));
  LED led_30 (.in(u_ROM_LED_Arranger_data[34]));
  LED led_31 (.in(u_ROM_LED_Arranger_data[7]));
  LED led_32 (.in(u_ROM_LED_Arranger_data[8]));
  LED led_33 (.in(u_ROM_LED_Arranger_data[31]));
  LED led_34 (.in(u_ROM_LED_Arranger_data[32]));
  LED led_35 (.in(u_ROM_LED_Arranger_data[5]));
  LED led_36 (.in(u_ROM_LED_Arranger_data[6]));
  LED led_37 (.in(u_ROM_LED_Arranger_data[29]));
  LED led_38 (.in(u_ROM_LED_Arranger_data[30]));
  LED led_39 (.in(u_ROM_LED_Arranger_data[3]));
  LED led_40 (.in(u_ROM_LED_Arranger_data[4]));
  LED led_41 (.in(u_ROM_LED_Arranger_data[27]));
  LED led_42 (.in(u_ROM_LED_Arranger_data[28]));
  LED led_43 (.in(u_ROM_LED_Arranger_data[1]));
  LED led_44 (.in(u_ROM_LED_Arranger_data[2]));
  LED led_45 (.in(u_ROM_LED_Arranger_data[25]));
  LED led_46 (.in(u_ROM_LED_Arranger_data[26]));
  LED led_47 (.in(u_ROM_LED_Arranger_data[0]));
  LED led_48 (.in(u_ROM_LED_Arranger_data[24]));
endmodule

/* Code of ROM_LED_Arranger:
library IEEE;
use IEEE.STD_LOGIC_1164.ALL;
use IEEE.NUMERIC_STD.ALL;

entity ROM_LED_Arranger is
    Port (
        EN       : in  STD_LOGIC;
        Mode     : in  STD_LOGIC_VECTOR(1 downto 0);
        Progress : in  STD_LOGIC_VECTOR(3 downto 0);
        Data     : out STD_LOGIC_VECTOR(47 downto 0)  -- 48 LED, upper row then lower row
    );
end ROM_LED_Arranger;

architecture Behavioral of ROM_LED_Arranger is

    -------------------------------------------------------------------------
    -- 24‑bit ROM type – one row (左到右編號：左端為高位元，右端為低位元)
    -------------------------------------------------------------------------
    type rom24_type is array (0 to 15) of std_logic_vector(23 downto 0);

    -- Row‑wise helper constants
    constant ALL_ON_24  : std_logic_vector(23 downto 0) := x"FFFFFF";  -- 24 個 1
    constant ALL_OFF_24 : std_logic_vector(23 downto 0) := x"000000";  -- 24 個 0

    -------------------------------------------------------------------------
    -- Mode 0 : idle – both rows always off
    -------------------------------------------------------------------------
    constant MODE0_UP_ROM  : rom24_type := (others => ALL_OFF_24);
    constant MODE0_LOW_ROM : rom24_type := (others => ALL_OFF_24);

    -------------------------------------------------------------------------
    -- Mode 1 : Fin = 3 – 右側每次清除 8 顆 LED (共 3 步)
    -------------------------------------------------------------------------
    constant MODE1_UP_ROM : rom24_type := (
        0 => ALL_ON_24,   -- 111111111111111111111111
        1 => x"FFFF00",   -- 右側 8 顆熄滅
        2 => x"FF0000",   -- 右側 16 顆熄滅
        3 => ALL_OFF_24,
        others => ALL_OFF_24
    );
    constant MODE1_LOW_ROM : rom24_type := (
        0 => ALL_ON_24,
        1 => x"FFFF00",
        2 => x"FF0000",
        3 => ALL_OFF_24,
        others => ALL_OFF_24
    );

    -------------------------------------------------------------------------
    -- Mode 2 : Fin = 6 – 右側每次清除 4 顆 LED (共 6 步)
    -------------------------------------------------------------------------
    constant MODE2_UP_ROM : rom24_type := (
        0 => ALL_ON_24,
        1 => x"FFFFF0",   -- clear 4 LSB
        2 => x"FFFF00",   -- clear 8 LSB
        3 => x"FFF000",   -- clear 12 LSB
        4 => x"FF0000",   -- clear 16 LSB
        5 => x"F00000",   -- clear 20 LSB
        6 => x"000000",   -- clear 24 LSB (全部熄滅)
        others => ALL_OFF_24
    );
    constant MODE2_LOW_ROM : rom24_type := (
        0 => ALL_ON_24,
        1 => x"FFFFF0",
        2 => x"FFFF00",
        3 => x"FFF000",
        4 => x"FF0000",
        5 => x"F00000",
        6 => x"000000",
        others => ALL_OFF_24
    );

    -------------------------------------------------------------------------
    -- Mode 3 : Fin = 12 – 右側每次清除 2 顆 LED (共 12 步)
    -------------------------------------------------------------------------
    constant MODE3_UP_ROM : rom24_type := (
        0  => ALL_ON_24,   -- 111111111111111111111111
        1  => x"FFFFFC",   -- clear 2 LSB
        2  => x"FFFFF0",   -- clear 4 LSB
        3  => x"FFFFC0",   -- clear 6 LSB
        4  => x"FFFF00",   -- clear 8 LSB
        5  => x"FFFC00",   -- clear 10 LSB
        6  => x"FFF000",   -- clear 12 LSB
        7  => x"FFC000",   -- clear 14 LSB
        8  => x"FF0000",   -- clear 16 LSB
        9  => x"FC0000",   -- clear 18 LSB
        10 => x"F00000",   -- clear 20 LSB
        11 => x"C00000",   -- clear 22 LSB
        others => ALL_OFF_24
    );
    constant MODE3_LOW_ROM : rom24_type := (
        0  => ALL_ON_24,
        1  => x"FFFFFC",
        2  => x"FFFFF0",
        3  => x"FFFFC0",
        4  => x"FFFF00",
        5  => x"FFFC00",
        6  => x"FFF000",
        7  => x"FFC000",
        8  => x"FF0000",
        9  => x"FC0000",
        10 => x"F00000",
        11 => x"C00000",
        others => ALL_OFF_24
    );

begin

    process(EN, Mode, Progress)
        variable idx : integer range 0 to 15;
        variable up_row  : std_logic_vector(23 downto 0);
        variable low_row : std_logic_vector(23 downto 0);
    begin
        idx := to_integer(unsigned(Progress));
        if EN = '0' then
            Data <= (others => '0');
        else
            case Mode is
                when "00" =>
                    up_row  := MODE0_UP_ROM(idx);
                    low_row := MODE0_LOW_ROM(idx);
                when "01" =>
                    up_row  := MODE1_UP_ROM(idx);
                    low_row := MODE1_LOW_ROM(idx);
                when "10" =>
                    up_row  := MODE2_UP_ROM(idx);
                    low_row := MODE2_LOW_ROM(idx);
                when "11" =>
                    up_row  := MODE3_UP_ROM(idx);
                    low_row := MODE3_LOW_ROM(idx);
                when others =>
                    up_row  := ALL_OFF_24;
                    low_row := ALL_OFF_24;
            end case;
            Data <= up_row & low_row;  -- upper row (bits 47..24) + lower row (bits 23..0)
        end if;
    end process;

end Behavioral;
*/
